# Fritzing sketch bus_mouse_tester (saved by Fritzing 0.9.2b)
circuit board: 8.46667cm x 5.64444cm

parts:
  Часть1 = Arduino Uno (Rev3)
  X2 = DB9 Connector [package=db9]

nets:
  N1: Часть1.GND, X2.8
  N2: Часть1.D0/RX, X2.6
  N3: Часть1.D1/TX, X2.5
  N4: Часть1.D2, X2.9
  N5: Часть1.D4, X2.4
  N6: Часть1.D5_PWM, X2.2
  N7: Часть1.D6_PWM, X2.1
  N8: Часть1.D7, X2.3
  N9: Часть1.5V, X2.7
